# Fritzing sketch Automatic Hand Washing Machine (saved by Fritzing 0.9.3b)

parts:
  Part1 = Arduino Uno (Rev3) - ICSP
  Q1 = TRANSISTOR_NPN [package=to-92]
  R1 = Resistor [tolerance=±5% resistance=220 package="0402 [SMD]"]
  M1 = DC Motor
  Part2 = SRF05 Ultrasonic Rangefinder

nets:
  N1: Part1.D13/SCK, R1.Pin_1
  N2: Part1.GND, Q1.E, Part2.connector11
  N3: Part1.D5_PWM, Part2.connector9
  N4: Part1.D6_PWM, Part2.connector10
  N5: Part1.5V, Part2.connector8
  N6: Q1.B, R1.Pin_0
  N7: Q1.C, M1.pin_1
